# Fritzing sketch GaragePiShield (saved by Fritzing 0.8.7b)
circuit board: 7cm x 5cm
breadboards: 1

parts:
  InGPIO = female pin header, 4 pins [form="♀ (female)"]
  InPwr = female pin header, 4 pins [form="♀ (female)"]
  S1 = Pushbutton [package="[THT]"]
  S2 = Pushbutton [package="[THT]"]
  S3 = Pushbutton [package="[THT]"]
  S4 = Pushbutton [package="[THT]"]
  R1 = Resistor [tolerance=±5% resistance=1k package=THT]
  R2 = Resistor [tolerance=±5% resistance=1k package=THT]
  R3 = Resistor [tolerance=±5% resistance=10k package=THT]
  R4 = Resistor [tolerance=±5% resistance=10k package=THT]
  R5 = Resistor [tolerance=±5% resistance=1k package=THT]
  R6 = Resistor [tolerance=±5% resistance=10k package=THT]
  R7 = Resistor [tolerance=±5% resistance=1k package=THT]
  R8 = Resistor [tolerance=±5% resistance=10k package=THT]
  R9 = Resistor [tolerance=±5% resistance=1k package=THT]
  R10 = Resistor [tolerance=±5% resistance=10k package=THT]
  Q1 = NPN-Transistor [package="TO92 [THT]"]
  L1 = Solenoid
  J1 = female pin header, 2 pins [form="♀ (female)"]
  R11 = Resistor [tolerance=±5% resistance=1k package=THT]
  R12 = Resistor [tolerance=±5% resistance=10k package=THT]
  Q2 = NPN-Transistor [package="TO92 [THT]"]
  L2 = Solenoid
  Raspberry_Pi_B_rev1 = Raspberry Pi B rev2
  J2 = female pin header, 2 pins [form="♀ (female)"]

nets:
  N1: InGPIO.pin1, S1.Pin_3, S1.Pin_4, R7.Pin_1, R8.Pin_0
  N2: InGPIO.pin2, S2.Pin_3, S2.Pin_4, R5.Pin_1, R6.Pin_0
  N3: InGPIO.pin3, S3.Pin_3, S3.Pin_4, R2.Pin_1, R3.Pin_0
  N4: InGPIO.pin4, S4.Pin_3, S4.Pin_4, R1.Pin_1, R4.Pin_0
  N5: InPwr.pin1, InPwr.pin2, InPwr.pin3, InPwr.pin4, S1.Pin_1, S1.Pin_2, S2.Pin_1, S2.Pin_2, S3.Pin_1, S3.Pin_2, S4.Pin_1, S4.Pin_2, Raspberry_Pi_B_rev1.3V3
  N6: R1.Pin_0, Raspberry_Pi_B_rev1.GPIO_3
  N7: R2.Pin_0, Raspberry_Pi_B_rev1.GPIO_4
  GND: R3.Pin_1, R4.Pin_1, R6.Pin_1, R8.Pin_1, R10.Pin_0, Q1.E, L1.pin2, R12.Pin_0, Q2.E, L2.pin2, Raspberry_Pi_B_rev1.GND, J2.pin1, J2.pin2
  N8: R5.Pin_0, Raspberry_Pi_B_rev1.GPIO_17
  N9: R7.Pin_0, Raspberry_Pi_B_rev1.GPIO_27
  N10: R9.Pin_0, R10.Pin_1, Q1.B
  N11: R9.Pin_1, Raspberry_Pi_B_rev1.GPIO_10
  N12: Q1.C, L1.pin1, J1.pin1
  N13: J1.pin2, Q2.C, L2.pin1
  N14: R11.Pin_0, R12.Pin_1, Q2.B
  N15: R11.Pin_1, Raspberry_Pi_B_rev1.GPIO_9
